# Fritzing sketch ESP8266 (saved by Fritzing 0.9.4)

parts:
  U1 = ESP8266 WiFi Module [part_number=ESP8266]
  SparkFun_RedBoard_Artemis1 = SparkFun RedBoard Artemis

nets:
  N1: U1.RXD, SparkFun_RedBoard_Artemis1.~D1/TXO-1
  VCC: U1.VCC, SparkFun_RedBoard_Artemis1.VDD
  N2: U1.RST, SparkFun_RedBoard_Artemis1.~D2/A6
  GND: U1.GND, SparkFun_RedBoard_Artemis1.GND
  N3: U1.TXD, SparkFun_RedBoard_Artemis1.~D0/RXI-1

custom parts:
  ESP8266 WiFi Module: Generic WiFi Module based on the ESP8266 with onboard PCB antenna and UART communications
  SparkFun RedBoard Artemis: Think of the RedBoard Artemis as just another Arduino... That has BLE. And one megabyte of flash. And runs at less than 1mA. Oh, and it can run TensorFlow models. Ya, that too. The RedBoard Artemis takes the incredibly powerful Artemis module from SparkFun and wraps it up in an easy to use and familiar Uno footprint. We've written an Arduino core from scratch to make programming the Artemis as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
